# Fritzing sketch sheet (saved by Fritzing 1.0.6)

parts:
  U1 = XIAO ESP32C6 [part_number=" XIAO ESP32C6"]
  A1 = GY-BMP280 Breakout
  R1 = Resistor [tolerance=±5% power=0.25W resistance=470 package=THT]
  R2 = Resistor [tolerance=±5% power=0.25W resistance=15 package=THT]
  LED1 = LED - 3mm [color="Infrared (940nm)" package="3 mm [THT]"]
  LED2 = LED - 3mm [color="Infrared (940nm)" current=0.030A package="3 mm [THT]"]
  Q1 = NPN-Transistor [part_number=2n5551 package="TO92 [THT]"]
  LED3 = LED - 3mm [color="Infrared (940nm)" current=0.030A package="3 mm [THT]"]

nets:
  N1: U1.D4, A1.Pin_4
  N2: U1.D5, A1.Pin_3
  N3: U1.D9, R1.Pin_0
  N4: U1.3V3, A1.Pin_1
  N5: U1.GND, A1.Pin_2, Q1.E
  N6: U1.5V, LED3.anode
  N7: R1.Pin_1, Q1.B
  N8: R2.Pin_0, Q1.C
  N9: R2.Pin_1, LED2.cathode
  N10: LED1.cathode, LED2.anode
  N11: LED1.anode, LED3.cathode

custom parts:
  XIAO ESP32C6: XIAO ESP32C6 is a cost-effective MCU based on Espressif’s ESP32-C6. This compact MCU excels in Matter-compliant smart home applications with its support for various wireless connectivity (2.4GHz Wi-Fi 6, BLE 5.0, Zigbee, and Thread). Designed with the thumb-size footprint and a single-sided mount of the XIAO Series, it's perfect for space-limited projects. Encrypted on the chip, the XIAO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
